// Logisim project cpu.circ as structural Verilog: 2 circuits, main circuit main
module main (
  input  [31:0] in_1,
  input  [20:0] in_2,
  input  in_3,
  input  in_4,
  output [31:0] out_5
);

  wire clock_1_out;

  Clock clock_1 (.out(clock_1_out));
  RAM_CONTROLLER ram_controller_1 (
    .WRITEIN(in_1), .ADDRESS(in_2), .WRITESTART(in_3), .READSTART(in_4), .CLK(clock_1_out), .READOUT(out_5));
endmodule

module RAM_CONTROLLER (
  input  [31:0] WRITEIN,
  input  [20:0] ADDRESS,
  input  WRITESTART,
  input  READSTART,
  input  CLK,
  output [31:0] READOUT
);

  wire and_1_out, and_2_out, and_3_out, d_ff_1_q, d_ff_2_q, d_ff_5_q, demultiplexer_1_out0,
       demultiplexer_1_out1, demultiplexer_2_out0, demultiplexer_2_out1, demultiplexer_2_out2,
       demultiplexer_2_out3, multiplexer_1_out, not_1_out, not_2_out, or_1_out, s_r_ff_1_q, xor_1_out,
       xor_2_out, xor_3_out;
  wire [1:0] d_ff_3_q;
  wire [7:0] multiplexer_2_out, RAM1_data;
  wire [20:0] adder_1_out;

  D_Flip_Flop d_ff_1 (.D(WRITESTART), .clk(CLK), .Q(d_ff_1_q));  // open: Qn, preset, reset
  D_Flip_Flop d_ff_2 (.D(READSTART), .clk(CLK), .Q(d_ff_2_q));  // open: Qn, preset, reset
  and and_1 (and_1_out, WRITESTART, not_1_out);
  not not_1 (not_1_out, d_ff_1_q);
  and and_2 (and_2_out, READSTART, not_2_out);
  not not_2 (not_2_out, d_ff_2_q);
  or or_1 (or_1_out, and_1_out, and_2_out);
  Multiplexer multiplexer_1 (.in0(d_ff_5_q), .in1(and_2_out), .out(multiplexer_1_out), .sel(or_1_out));
  D_Flip_Flop d_ff_3 (.D(xor_1_out), .clk(CLK), .Q(d_ff_3_q[0]), .reset(xor_3_out));  // open: Qn, preset
  xor xor_1 (xor_1_out, d_ff_3_q[0], 1'b1);
  D_Flip_Flop d_ff_4 (.D(xor_2_out), .clk(CLK), .Q(d_ff_3_q[1]), .reset(xor_3_out));  // open: Qn, preset
  xor xor_2 (xor_2_out, d_ff_3_q[1], d_ff_3_q[0]);
  Adder #(.width(21)) adder_1 (.a({{19{1'b0}}, d_ff_3_q}), .b(ADDRESS), .out(adder_1_out), .cin(1'b0));  // open: cout
  S_R_Flip_Flop s_r_ff_1 (.S(or_1_out), .R(and_3_out), .clk(CLK), .Q(s_r_ff_1_q));  // open: reset, Qn, preset
  D_Flip_Flop d_ff_5 (.D(multiplexer_1_out), .clk(CLK), .Q(d_ff_5_q));  // open: Qn, preset, reset
  xor xor_3 (xor_3_out, 1'b1, s_r_ff_1_q);
  and and_3 (and_3_out, d_ff_3_q[0], d_ff_3_q[1]);
  Demultiplexer demultiplexer_1 (
    .out0(demultiplexer_1_out0), .out1(demultiplexer_1_out1), .in(s_r_ff_1_q), .sel(d_ff_5_q));
  RAM #(.addrWidth(21), .asyncread("true"), .databus("bidir")) RAM1 (
    .addr(adder_1_out), .we(demultiplexer_1_out0), .oe(demultiplexer_1_out1), .clk(CLK), .data(RAM1_data));
  Multiplexer #(.select(2), .width(8)) multiplexer_2 (
    .in0(WRITEIN[31:24]), .in1(WRITEIN[23:16]), .in2(WRITEIN[15:8]), .in3(WRITEIN[7:0]),
    .out(multiplexer_2_out), .sel(d_ff_3_q));
  assign RAM1_data = demultiplexer_1_out0 ? multiplexer_2_out : 8'bz;  // Controlled_Buffer controlled_buffer_1
  Demultiplexer #(.select(2)) demultiplexer_2 (
    .out0(demultiplexer_2_out0), .out1(demultiplexer_2_out1), .out2(demultiplexer_2_out2),
    .out3(demultiplexer_2_out3), .in(demultiplexer_1_out1), .sel(d_ff_3_q));
  Register register_1 (.D(RAM1_data), .en(demultiplexer_2_out0), .clk(CLK), .Q(READOUT[31:24]));  // open: clr
  Register register_2 (.D(RAM1_data), .en(demultiplexer_2_out1), .clk(CLK), .Q(READOUT[23:16]));  // open: clr
  Register register_3 (.D(RAM1_data), .en(demultiplexer_2_out2), .clk(CLK), .Q(READOUT[15:8]));  // open: clr
  Register register_4 (.D(RAM1_data), .en(demultiplexer_2_out3), .clk(CLK), .Q(READOUT[7:0]));  // open: clr
endmodule
